# Fritzing sketch soul-dancer (saved by Fritzing 0.9.3b)
breadboards: 1

parts:
  Part1 = Arduino Mega 2560 (Rev3)
  U1 = 2.5mm Audio Jack [package=stereojack2.5mm_specia_pogopins]
  C2 = Ceramic Capacitor [capacitance=4.7µF package="100 mil [THT, multilayer]"]
  R1 = Resistor [tolerance=±5% resistance=100k package="0402 [SMD]"]
  R3 = Resistor [tolerance=±5% resistance=100k package="0402 [SMD]"]
  R4 = TRIMPOT [package=trimpot_tc33]
  ArmsR1 = Basic Servo
  ArmsR2 = Basic Servo
  Turn = Basic Servo
  Part3 = Adafruit Audio FX Mini Sound Board [part_number="Adafruit #2342 and #2220"]
  Speaker = SPEAKER [package=pcb_mount_speaker]
  Turn1 = Basic Servo
  C4 = Electrolytic Capacitor [capacitance=1µF package="100 mil [THT, electrolytic]"]
  Part7 = Adafruit LM3671 Buck Converter [part_number=DFR0379]
  PAM8302 = Mono 2.5W Class D Audio Amplifier - PAM8302
  Ultrasonic_sensor = hc-sr04
  Part8 = SM 5050 [package=THT]

nets:
  GND: Part1.GND, U1.SLEEVE, C2.0, R3.Pin_0, ArmsR1.gnd, ArmsR2.gnd, Turn.gnd, Part3.GND, Turn1.gnd, Part7.GND, PAM8302.GND, PAM8302.AIN-, Ultrasonic_sensor.GND, Part8.R
  N1: Part1.D13_PWM, ArmsR1.pulse
  N2: Part1.D12_PWM, ArmsR2.pulse
  N3: Part1.D11_PWM, Turn.pulse
  N4: Part1.D10_PWM, Turn1.pulse
  N5: Part1.5V, R1.Pin_1
  12V: Part1.VIN, Part7.VIN
  N6: Part1.D6_PWM, Ultrasonic_sensor.Echo
  N7: Part1.D7_PWM, Ultrasonic_sensor.Trig
  N8: Part1.D22, Part8.VCC
  N9: Part1.D38, Part3.GPIO0_0
  N10: Part1.D40, Part3.GPIO0_2
  N11: Part1.D42, Part3.GPIO0_4
  N12: Part1.D45, Part3.GPIO0_7
  N13: U1.LEFT, U1.RIGHT, C4.+
  N14: C2.1, R4.WIPER, C4.-
  N15: R1.Pin_0, R4.CCW
  N16: R3.Pin_1, R4.CW
  VCC: ArmsR1.vcc, ArmsR2.vcc, Turn.vcc, Turn1.vcc
  VIN: Part3.VIN, PAM8302.VCC
  N17: Part3.L_AC, PAM8302.AIN+
  N18: Speaker.+, PAM8302.VO+
  N19: Speaker.-, PAM8302.VO-
  3.3V: Part7.3.3V, Ultrasonic_sensor.VCC

notes:
  We use DFR0379 instead of the Adafruit LM3671 - it outputs 5v at 3A max
  We use a generic RGB led strip that uses SM5050 leds instead of the W5281b leds

custom parts:
  Adafruit Audio FX Mini Sound Board: Would you like to add audio/sound effects to your next project, without an Arduino+Shield? Or maybe you don't even know how to use microcontrollers, you just want to make a sound play whenever you press a button. What about something that has to be very small and portable? You are probably feeling a little frustrated: it's been very hard to find a simple, low cost audio effects trigger that is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
  Adafruit LM3671 Buck Converter: Your power supply problems just got SUPER SOLVED! This 3.3V Buck Converter Breakout board is great for supplying power to low voltage circuits from a single Li-Ion cell battery or USB power. This chip provides up to 600-mA load current across the entire input voltage range of 3.5 to 5.5V. Great for your portable project, we made this "pin compatible" with the LM1117-3.3V TO-220 chip so you can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
  Mono 2.5W Class D Audio Amplifier - PAM8302: A super small but powerful mono amplifier able to deliver up to 2.5 Watts into 4-8 ohm impedance speakers. Inside the miniature chip is a class D controller, able to run from 2.0V-5.5VDC. Since the amp is a class D, its very efficient (over 90% efficient when driving an 8Ω speaker at over half a Watt) - making it perfect for portable and battery-powered projects.
  hc-sr04: This is a HC-SR04 Distance Sensor
  SM 5050: SM 5050 LED strip
